// Logisim project L13P66.circ as structural Verilog: 1 circuit, main circuit main
module main (
  input  En
);

  wire and_1_out, and_2_out, and_3_out, and_4_out, and_5_out, and_6_out, clock_1_out, d_ff_1_qn, d_ff_2_q,
       d_ff_2_qn, d_ff_3_q, d_ff_3_qn, d_ff_4_q, d_ff_4_qn, not_1_out, not_2_out, not_3_out, or_1_out,
       shift_register_1_out;

  Clock clock_1 (.out(clock_1_out));
  Shift_Register shift_register_1 (
    .clk(and_1_out), .out(shift_register_1_out));  // open: shift, in, load, clr, d0, q0, d1, q1, d2, q2, d3, q3, d4, q4, d5, q5, d6, q6, d7, q7
  and and_1 (and_1_out, clock_1_out, En);
  and and_2 (and_2_out, and_1_out, and_5_out);
  D_Flip_Flop d_ff_1 (.clk(and_2_out), .D(and_5_out), .Qn(d_ff_1_qn));  // open: Q, preset, en, reset
  and and_3 (and_3_out, d_ff_3_qn, d_ff_2_q, not_1_out, d_ff_1_qn, d_ff_4_qn);
  not not_1 (not_1_out, shift_register_1_out);
  D_Flip_Flop d_ff_2 (.clk(and_1_out), .D(and_4_out), .Q(d_ff_2_q), .Qn(d_ff_2_qn));  // open: preset, en, reset
  and and_4 (and_4_out, shift_register_1_out, d_ff_3_q);
  LED Z1 (.in(and_3_out));
  not not_2 (not_2_out, shift_register_1_out);
  D_Flip_Flop d_ff_3 (.clk(and_1_out), .D(not_2_out), .Q(d_ff_3_q), .Qn(d_ff_3_qn));  // open: preset, en, reset
  not not_3 (not_3_out, shift_register_1_out);
  or or_1 (or_1_out, d_ff_2_q, d_ff_4_q, shift_register_1_out);
  and and_5 (and_5_out, not_3_out, d_ff_2_qn, d_ff_3_q, d_ff_4_q);
  LED Z2 (.in(and_5_out));
  and and_6 (and_6_out, or_1_out, d_ff_3_qn);
  D_Flip_Flop d_ff_4 (.clk(and_1_out), .D(and_6_out), .Q(d_ff_4_q), .Qn(d_ff_4_qn));  // open: preset, en, reset

  // Notes on the sheet:
  //   A
  //   B
  //   C
endmodule
